// Logisim project LOGIC DECODER FOR 7-SEGMENT DISPLAY (WITH GRAY-COUNTER).circ as structural Verilog: 1 circuit, main circuit main
module main (
  output out_1,
  output out_2,
  output out_3,
  output out_4,
  output out_5,
  output out_6,
  output out_7,
  output out_8
);

  wire a_out, A_prime_B_out, A_prime_B_prime_C_out, A_prime_B_prime_out, A_prime_BC_prime_D_out,
       A_prime_BC_prime_out, A_prime_C_out, A_prime_C_prime_D_prime_out, A_prime_C_prime_out, A_prime_CD_out,
       A_prime_D_out, AB_out, AB_prime_C_prime_out, AB_prime_out, ABC_prime_out, AC_out, AC_prime_D_out,
       AD_out, AD_prime_out, and_1_out, and_2_out, and_3_out, and_4_out, b_out,
       B_prime_C_prime_D_prime_2_out, B_prime_C_prime_D_prime_out, B_prime_CD_out, B_prime_D_prime_out,
       BC_prime_D_out, BCD_prime_2_out, BCD_prime_out, c_out, C_prime_B_prime_out, C_prime_D_out,
       C_prime_D_prime_out, CB_out, CD_prime_out, d_out, e_out, f_out, g_out, j_k_ff_1_qn, j_k_ff_2_qn,
       j_k_ff_3_qn, not_1_out, not_2_out, not_3_out, not_4_out, not_5_out, not_6_out, not_7_out, not_8_out,
       not_9_out, not_10_out, not_11_out, not_12_out, not_13_out, not_14_out, not_15_out, not_16_out,
       xnor_1_out, xor_1_out;

  Clock clock_1 (.out(out_4));
  xnor xnor_1 (xnor_1_out, out_2, out_3);
  xor xor_1 (xor_1_out, out_2, out_3);
  not not_1 (not_1_out, out_4);
  not not_2 (not_2_out, out_1);
  not not_3 (not_3_out, out_2);
  not not_4 (not_4_out, out_3);
  J_K_Flip_Flop j_k_ff_1 (
    .J(xnor_1_out), .clk(out_4), .K(xor_1_out), .Q(out_1), .Qn(j_k_ff_1_qn));  // open: preset, en, reset
  and and_1 (and_1_out, out_1, j_k_ff_3_qn);
  and and_2 (and_2_out, out_1, out_3);
  J_K_Flip_Flop j_k_ff_2 (
    .J(and_1_out), .clk(out_4), .K(and_2_out), .Q(out_2), .Qn(j_k_ff_2_qn));  // open: preset, en, reset
  not not_5 (not_5_out, not_3_out);
  not not_6 (not_6_out, not_4_out);
  and A_prime_B_prime (A_prime_B_prime_out, not_3_out, not_4_out);
  not not_7 (not_7_out, not_3_out);
  and C_prime_B_prime (C_prime_B_prime_out, not_3_out, not_2_out);
  not not_8 (not_8_out, not_2_out);
  and A_prime_CD (A_prime_CD_out, not_4_out, out_1, out_4);
  and A_prime_C_prime_D_prime (A_prime_C_prime_D_prime_out, not_4_out, not_2_out, not_1_out);
  not not_9 (not_9_out, out_1);
  and CD_prime (CD_prime_out, out_1, not_1_out);
  not not_10 (not_10_out, not_1_out);
  and AB_prime_C_prime (AB_prime_C_prime_out, out_3, not_3_out, not_2_out);
  not not_11 (not_11_out, out_3);
  and AD_prime (AD_prime_out, out_3, not_1_out);
  not not_12 (not_12_out, not_1_out);
  and AB_prime (AB_prime_out, out_3, not_3_out);
  not not_13 (not_13_out, out_3);
  not not_14 (not_14_out, not_3_out);
  and A_prime_C_prime (A_prime_C_prime_out, not_4_out, not_2_out);
  and A_prime_B_prime_C (A_prime_B_prime_C_out, not_4_out, not_3_out, out_1);
  and A_prime_BC_prime_D (A_prime_BC_prime_D_out, not_4_out, out_2, not_2_out, out_4);
  and A_prime_C (A_prime_C_out, not_4_out, out_1);
  and B_prime_D_prime (B_prime_D_prime_out, not_1_out, not_3_out);
  not not_15 (not_15_out, not_1_out);
  not not_16 (not_16_out, not_3_out);
  and B_prime_CD (B_prime_CD_out, not_3_out, out_1, out_4);
  and AC (AC_out, out_3, out_1);
  and ABC_prime (ABC_prime_out, out_3, out_2, not_2_out);
  and BCD_prime (BCD_prime_out, out_2, out_1, not_1_out);
  and A_prime_BC_prime (A_prime_BC_prime_out, not_4_out, out_2, not_2_out);
  and AD (AD_out, out_3, out_4);
  and C_prime_D_prime (C_prime_D_prime_out, not_1_out, not_2_out);
  and and_3 (and_3_out, out_2, j_k_ff_1_qn);
  and and_4 (and_4_out, j_k_ff_1_qn, j_k_ff_2_qn);
  and AB (AB_out, not_5_out, not_6_out);
  and CB (CB_out, not_7_out, not_8_out);
  and C_prime_D (C_prime_D_out, not_9_out, not_10_out);
  and A_prime_D (A_prime_D_out, not_11_out, not_12_out);
  and A_prime_B (A_prime_B_out, not_13_out, not_14_out);
  and BCD_prime_2 (BCD_prime_2_out, CB_out, not_1_out);
  and B_prime_C_prime_D_prime (B_prime_C_prime_D_prime_out, B_prime_D_prime_out, not_2_out);
  and BC_prime_D (BC_prime_D_out, not_15_out, not_16_out, not_2_out);
  and AC_prime_D (AC_prime_D_out, AD_out, not_2_out);
  and B_prime_C_prime_D_prime_2 (B_prime_C_prime_D_prime_2_out, C_prime_D_prime_out, not_3_out);
  J_K_Flip_Flop j_k_ff_3 (
    .J(and_3_out), .clk(out_4), .K(and_4_out), .Q(out_3), .Qn(j_k_ff_3_qn));  // open: preset, en, reset
  or b (b_out, AC_prime_D_out, A_prime_B_prime_out, B_prime_D_prime_out, A_prime_CD_out, A_prime_C_prime_D_prime_out, C_prime_B_prime_out);
  or a (a_out, B_prime_D_prime_out, CB_out, A_prime_C_out, AD_prime_out, AB_prime_C_prime_out, A_prime_BC_prime_D_out);
  or c (c_out, C_prime_D_out, AB_prime_out, A_prime_C_prime_out, A_prime_B_out, A_prime_D_out);
  or d (d_out, B_prime_CD_out, BCD_prime_2_out, A_prime_B_prime_C_out, ABC_prime_out, BC_prime_D_out, B_prime_C_prime_D_prime_out);
  or e (e_out, CD_prime_out, AB_out, AC_out, B_prime_C_prime_D_prime_2_out);
  or f (f_out, C_prime_D_prime_out, AC_out, AB_prime_out, A_prime_BC_prime_out, BCD_prime_out);
  or g (g_out, CD_prime_out, AB_prime_out, AD_out, A_prime_BC_prime_out, B_prime_CD_out);
  _7_Segment_Display u_7_segment_display_1 (
    .g(g_out), .f(f_out), .a(a_out), .b(b_out), .e(e_out), .d(d_out), .c(c_out), .dp(out_4));

  assign out_5 = out_3;
  assign out_6 = out_2;
  assign out_7 = out_1;
  assign out_8 = out_4;

  // Notes on the sheet:
  //   D
  //   C
  //   B
  //   A
  //   10=A
  //   11=b
  //   12=C
  //   13=d
  //   14=E
  //   15=F
  //   By Faury A. Abreu
endmodule
